# Fritzing sketch breadboard-design (saved by Fritzing 0.9.3b)
perfboards: 1
breadboards: 1

parts:
  J1 = female pin header, 2 pins [form="♀ (female)"]  # not connected
  J2 = female pin header, 2 pins [form="♀ (female)"]
  LowHeader = Header 12 [package=1x12_machine-pin-header_lock.004]
  JP3 = Header 12 [package=1x12_machine-pin-header_lock.004]
  U3 = Voltage Regulator - 5V [package="DPak [SMD]"]
  J3 = female pin header, 2 pins [form="♀ (female)"]
  J4 = female pin header, 2 pins [form="♀ (female)"]
  Q1 = Basic FET N-Channel [package="DPak [SMD]"]

nets:
  N1: J2.pin1, U3.output_voltage
  N2: J2.pin2, LowHeader.gnd
  N3: LowHeader.1, J3.pin2
  N4: LowHeader.9, Q1.source
  N5: JP3.3v, U3.input_voltage
  N6: JP3.12, J4.pin1

custom parts:
  Header 12: Header 12 Standard 12-pin 0.1 header. Use with straight break away headers (SKU : PRT-00116), right angle break away headers (PRT-00553), swiss pins (PRT-00743), machine pins (PRT-00117), and female headers (PRT-00115).
  Header 12: Header 12 Standard 12-pin 0.1 header. Use with straight break away headers (SKU : PRT-00116), right angle break away headers (PRT-00553), swiss pins (PRT-00743), machine pins (PRT-00117), and female headers (PRT-00115).
